# Fritzing sketch meter_diagram (saved by Fritzing 0.9.2b)
breadboards: 1

parts:
  Arduino_UNO_or_Compatible = Arduino Uno (Rev3)
  CPU_METER = mystery part, 2 pins [chip_label="5V Galvanometer"]
  DISK_METER = mystery part, 2 pins [chip_label="5V Galvanometer"]
  MEMORY_METER = mystery part, 2 pins [chip_label="5V Galvanometer"]

nets:
  N1: Arduino_UNO_or_Compatible.A3, CPU_METER.pin1
  N2: Arduino_UNO_or_Compatible.D10_PWM/SS, DISK_METER.pin1
  N3: Arduino_UNO_or_Compatible.D11_PWM/MOSI, MEMORY_METER.pin1
  N4: Arduino_UNO_or_Compatible.GND, CPU_METER.pin2, DISK_METER.pin2, MEMORY_METER.pin2
